# Fritzing sketch WiringDiagram (saved by Fritzing 0.7.10b)
breadboards: 1

parts:
  Teensy++1 = Teensy++ 2.0
  S2 = Pushbutton [package=THT]
  S3 = Pushbutton [package=THT]
  LED1 = LED - 5mm [color="Orange (620nm)" package="5 mm [THT]"]
  LED2 = LED - 5mm [color="Orange (620nm)" package="5 mm [THT]"]
  LED3 = LED - 5mm [color="Orange (620nm)" package="5 mm [THT]"]
  LED4 = LED - 5mm [color="Orange (620nm)" package="5 mm [THT]"]
  LED5 = LED - 5mm [color="Orange (620nm)" package="5 mm [THT]"]
  LED6 = LED - 5mm [color="Orange (620nm)" package="5 mm [THT]"]
  LED7 = LED - 5mm [color="Red (633nm)" package="5 mm [THT]"]
  R1 = Resistor [tolerance=±5% resistance=220 package=THT]
  R2 = Resistor [tolerance=±5% resistance=220 package=THT]
  R3 = Resistor [tolerance=±5% resistance=220 package=THT]
  R4 = Resistor [tolerance=±5% resistance=220 package=THT]
  R5 = Resistor [tolerance=±5% resistance=220 package=THT]
  R6 = Resistor [tolerance=±5% resistance=220 package=THT]
  R7 = Resistor [tolerance=±5% resistance=220 package=THT]

nets:
  N1: Teensy++1.GND#0, Teensy++1.GND#21, S2.leg0, S3.leg0, R1.Pin_1, R2.Pin_1, R3.Pin_1, R4.Pin_1, R5.Pin_1, R6.Pin_1, R7.Pin_1
  N2: Teensy++1.D0, LED7.anode
  N3: Teensy++1.D2, LED1.anode
  N4: Teensy++1.D3, LED2.anode
  N5: Teensy++1.D4, LED6.anode
  N6: Teensy++1.D5, LED3.anode
  N7: Teensy++1.D6, LED5.anode
  N8: Teensy++1.D7, LED4.anode
  N9: Teensy++1.B0, S3.leg1
  N10: Teensy++1.B1, S2.leg1
  N11: LED1.cathode, R6.Pin_0
  N12: LED2.cathode, R7.Pin_0
  N13: LED3.cathode, R2.Pin_0
  N14: LED4.cathode, R3.Pin_0
  N15: LED5.cathode, R4.Pin_0
  N16: LED6.cathode, R5.Pin_0
  N17: LED7.cathode, R1.Pin_0

notes:
  Master
  Caution
  Reset
  System
  Annc
  Recall
  MC FLT IRS FUEL ELEC APU OVHT
